// Logisim project Roni_1908024_SAP1_with_Control_sequencer.circ as structural Verilog: 10 circuits, main circuit main
module main (
  input  [7:0] in_1,
  input  in_2,
  input  in_3,
  input  in_4,
  input  [7:0] in_5,
  input  in_6,
  input  in_7,
  input  [7:0] in_8,
  input  [7:0] in_9,
  input  in_10,
  input  in_11,
  input  in_12,
  input  in_13,
  input  [7:0] in_14,
  input  in_15,
  input  in_16,
  input  in_17,
  input  in_18,
  input  in_19,
  output [7:0] out_20,
  output [7:0] out_21,
  output out_22,
  output [7:0] out_23,
  output [7:0] out_24,
  output [3:0] out_25
);

  wire [7:0] gp_register_2_reg_in_out, gp_register_3_reg_in_out;

  GP_register gp_register_1 (
    .reg_in(in_1), .Reg_in_en(in_2), .Reg_clk(in_3), .Reg_out_en(in_4), .Reg_in_out(out_20), .Reg_out(out_21));
  Program_counter program_counter_1 (
    .in_1(in_16), .PC_clk(in_17), .PC_reset(in_18), .pc_out_en(in_19), .pc_out(out_25));
  ALU alu_1 (
    .alu_in_1(in_5), .alu_out_en(in_6), .alu_sub(in_7), .alu_in_2(in_8), .alu_carry_out(out_22),
    .alu_out(out_23));
  GP_register gp_register_2 (
    .reg_in(in_9), .Reg_in_en(in_10), .Reg_clk(in_11), .Reg_in_out(gp_register_2_reg_in_out));  // open: Reg_out_en, Reg_out
  GP_register gp_register_3 (
    .reg_in(in_14), .Reg_in_en(in_15), .Reg_clk(in_11), .Reg_in_out(gp_register_3_reg_in_out));  // open: Reg_out_en, Reg_out
  ALU alu_2 (
    .alu_in_1(gp_register_2_reg_in_out), .alu_out_en(in_12), .alu_sub(in_13),
    .alu_in_2(gp_register_3_reg_in_out), .alu_out(out_24));  // open: alu_carry_out
endmodule

module GP_register (
  input  [7:0] reg_in,
  input  Reg_in_en,
  input  Reg_clk,
  input  Reg_out_en,
  output [7:0] Reg_in_out,
  output [7:0] Reg_out
);

  wire multiplexer_1_out, multiplexer_2_out, multiplexer_3_out, multiplexer_4_out, multiplexer_5_out,
       multiplexer_6_out, multiplexer_7_out, multiplexer_8_out;

  Multiplexer multiplexer_1 (.in0(Reg_in_out[7]), .in1(reg_in[7]), .out(multiplexer_1_out), .sel(Reg_in_en));
  D_Flip_Flop d_ff_1 (.D(multiplexer_1_out), .clk(Reg_clk), .Q(Reg_in_out[7]));  // open: Qn, preset, reset
  Multiplexer multiplexer_2 (.in0(Reg_in_out[6]), .in1(reg_in[6]), .out(multiplexer_2_out), .sel(Reg_in_en));
  assign Reg_out[7] = Reg_out_en ? Reg_in_out[7] : 1'bz;  // Controlled_Buffer controlled_buffer_1
  D_Flip_Flop d_ff_2 (.D(multiplexer_2_out), .clk(Reg_clk), .Q(Reg_in_out[6]));  // open: Qn, preset, reset
  assign Reg_out[6] = Reg_out_en ? Reg_in_out[6] : 1'bz;  // Controlled_Buffer controlled_buffer_2
  Multiplexer multiplexer_3 (.in0(Reg_in_out[5]), .in1(reg_in[5]), .out(multiplexer_3_out), .sel(Reg_in_en));
  D_Flip_Flop d_ff_3 (.D(multiplexer_3_out), .clk(Reg_clk), .Q(Reg_in_out[5]));  // open: Qn, preset, reset
  assign Reg_out[5] = Reg_out_en ? Reg_in_out[5] : 1'bz;  // Controlled_Buffer controlled_buffer_3
  Multiplexer multiplexer_4 (.in0(Reg_in_out[4]), .in1(reg_in[4]), .out(multiplexer_4_out), .sel(Reg_in_en));
  D_Flip_Flop d_ff_4 (.D(multiplexer_4_out), .clk(Reg_clk), .Q(Reg_in_out[4]));  // open: Qn, preset, reset
  Multiplexer multiplexer_5 (.in0(Reg_in_out[3]), .in1(reg_in[3]), .out(multiplexer_5_out), .sel(Reg_in_en));
  assign Reg_out[4] = Reg_out_en ? Reg_in_out[4] : 1'bz;  // Controlled_Buffer controlled_buffer_4
  D_Flip_Flop d_ff_5 (.D(multiplexer_5_out), .clk(Reg_clk), .Q(Reg_in_out[3]));  // open: Qn, preset, reset
  Multiplexer multiplexer_6 (.in0(Reg_in_out[2]), .in1(reg_in[2]), .out(multiplexer_6_out), .sel(Reg_in_en));
  assign Reg_out[3] = Reg_out_en ? Reg_in_out[3] : 1'bz;  // Controlled_Buffer controlled_buffer_5
  D_Flip_Flop d_ff_6 (.D(multiplexer_6_out), .clk(Reg_clk), .Q(Reg_in_out[2]));  // open: Qn, preset, reset
  assign Reg_out[2] = Reg_out_en ? Reg_in_out[2] : 1'bz;  // Controlled_Buffer controlled_buffer_6
  Multiplexer multiplexer_7 (.in0(Reg_in_out[1]), .in1(reg_in[1]), .out(multiplexer_7_out), .sel(Reg_in_en));
  D_Flip_Flop d_ff_7 (.D(multiplexer_7_out), .clk(Reg_clk), .Q(Reg_in_out[1]));  // open: Qn, preset, reset
  assign Reg_out[1] = Reg_out_en ? Reg_in_out[1] : 1'bz;  // Controlled_Buffer controlled_buffer_7
  Multiplexer multiplexer_8 (.in0(Reg_in_out[0]), .in1(reg_in[0]), .out(multiplexer_8_out), .sel(Reg_in_en));
  D_Flip_Flop d_ff_8 (.D(multiplexer_8_out), .clk(Reg_clk), .Q(Reg_in_out[0]));  // open: Qn, preset, reset
  assign Reg_out[0] = Reg_out_en ? Reg_in_out[0] : 1'bz;  // Controlled_Buffer controlled_buffer_8
endmodule

module ALU (
  input  [7:0] alu_in_1,
  input  alu_out_en,
  input  alu_sub,
  input  [7:0] alu_in_2,
  output alu_carry_out,
  output [7:0] alu_out
);

  wire adder_2_cout, adder_3_cout, adder_4_cout, adder_5_cout, adder_6_cout, adder_7_cout, adder_8_cout,
       xor_1_out, xor_2_out, xor_3_out, xor_4_out, xor_5_out, xor_6_out, xor_7_out, xor_8_out;
  wire [7:0] adder_8_out;

  xor xor_1 (xor_1_out, alu_in_2[7], alu_sub);
  Adder #(.width(1)) adder_1 (
    .a(alu_in_1[7]), .b(xor_1_out), .out(adder_8_out[7]), .cin(adder_2_cout), .cout(alu_carry_out));
  xor xor_2 (xor_2_out, alu_in_2[6], alu_sub);
  Adder #(.width(1)) adder_2 (
    .a(alu_in_1[6]), .b(xor_2_out), .out(adder_8_out[6]), .cin(adder_3_cout), .cout(adder_2_cout));
  xor xor_3 (xor_3_out, alu_in_2[5], alu_sub);
  Adder #(.width(1)) adder_3 (
    .a(alu_in_1[5]), .b(xor_3_out), .out(adder_8_out[5]), .cin(adder_4_cout), .cout(adder_3_cout));
  xor xor_4 (xor_4_out, alu_in_2[4], alu_sub);
  Adder #(.width(1)) adder_4 (
    .a(alu_in_1[4]), .b(xor_4_out), .out(adder_8_out[4]), .cin(adder_5_cout), .cout(adder_4_cout));
  Adder #(.width(1)) adder_5 (
    .a(alu_in_1[3]), .b(xor_5_out), .out(adder_8_out[3]), .cin(adder_6_cout), .cout(adder_5_cout));
  xor xor_5 (xor_5_out, alu_in_2[3], alu_sub);
  xor xor_6 (xor_6_out, alu_in_2[2], alu_sub);
  Adder #(.width(1)) adder_6 (
    .a(alu_in_1[2]), .b(xor_6_out), .out(adder_8_out[2]), .cin(adder_7_cout), .cout(adder_6_cout));
  xor xor_7 (xor_7_out, alu_in_2[1], alu_sub);
  Adder #(.width(1)) adder_7 (
    .a(alu_in_1[1]), .b(xor_7_out), .out(adder_8_out[1]), .cin(adder_8_cout), .cout(adder_7_cout));
  Adder #(.width(1)) adder_8 (.a(alu_in_1[0]), .b(xor_8_out), .out(adder_8_out[0]), .cin(alu_sub), .cout(adder_8_cout));
  xor xor_8 (xor_8_out, alu_in_2[0], alu_sub);
  assign alu_out = alu_out_en ? adder_8_out : 8'bz;  // Controlled_Buffer controlled_buffer_1
endmodule

module Program_counter (
  input  in_1,
  input  PC_clk,
  input  PC_reset,
  input  pc_out_en,
  output [3:0] pc_out
);

  wire j_k_ff_2_qn, j_k_ff_3_qn, j_k_ff_4_qn;
  wire [3:0] j_k_ff_4_q;

  J_K_Flip_Flop j_k_ff_1 (
    .J(in_1), .K(in_1), .clk(j_k_ff_2_qn), .Q(j_k_ff_4_q[3]), .reset(PC_reset));  // open: Qn, preset
  J_K_Flip_Flop j_k_ff_2 (
    .J(in_1), .K(in_1), .clk(j_k_ff_3_qn), .Q(j_k_ff_4_q[2]), .Qn(j_k_ff_2_qn), .reset(PC_reset));  // open: preset
  J_K_Flip_Flop j_k_ff_3 (
    .J(in_1), .K(in_1), .clk(j_k_ff_4_qn), .Q(j_k_ff_4_q[1]), .Qn(j_k_ff_3_qn), .reset(PC_reset));  // open: preset
  J_K_Flip_Flop j_k_ff_4 (
    .J(in_1), .K(in_1), .clk(PC_clk), .Q(j_k_ff_4_q[0]), .Qn(j_k_ff_4_qn), .reset(PC_reset));  // open: preset
  assign pc_out = pc_out_en ? j_k_ff_4_q : 4'bz;  // Controlled_Buffer controlled_buffer_1
endmodule

module Dec_4_to_16 (
  input  [3:0] in_1,
  output [15:0] out_2
);

  wire not_1_out, not_2_out, not_3_out, not_4_out;

  not not_1 (not_1_out, in_1[3]);
  not not_2 (not_2_out, in_1[2]);
  not not_3 (not_3_out, in_1[1]);
  not not_4 (not_4_out, in_1[0]);
  and and_1 (out_2[0], not_4_out, not_3_out, not_2_out, not_1_out);
  and and_2 (out_2[1], in_1[0], not_3_out, not_2_out, not_1_out);
  and and_3 (out_2[2], not_4_out, in_1[1], not_2_out, not_1_out);
  and and_4 (out_2[3], in_1[0], in_1[1], not_2_out, not_1_out);
  and and_5 (out_2[4], not_4_out, not_3_out, in_1[2], not_1_out);
  and and_6 (out_2[5], in_1[0], not_3_out, in_1[2], not_1_out);
  and and_7 (out_2[6], not_4_out, in_1[1], in_1[2], not_1_out);
  and and_8 (out_2[7], in_1[0], in_1[1], in_1[2], not_1_out);
  and and_9 (out_2[8], not_4_out, not_3_out, not_2_out, in_1[3]);
  and and_10 (out_2[9], in_1[0], not_3_out, in_1[3]);
  and and_11 (out_2[10], not_4_out, in_1[1], not_2_out, in_1[3]);
  and and_12 (out_2[11], in_1[0], in_1[1], not_2_out, in_1[3]);
  and and_13 (out_2[12], not_4_out, not_3_out, in_1[2], in_1[3]);
  and and_14 (out_2[13], in_1[0], not_3_out, in_1[2], in_1[3]);
  and and_15 (out_2[14], not_4_out, in_1[1], in_1[2], in_1[3]);
  and and_16 (out_2[15], in_1[0], in_1[1], in_1[2], in_1[3]);
endmodule

module SRAM_cell (
  input  [7:0] data_in,
  input  wr_in,
  input  clk,
  input  cs,
  input  rd_en,
  output [7:0] mem_content,
  output [7:0] data_out
);

  wire and_1_out, and_2_out;

  and and_1 (and_1_out, wr_in, cs);
  and and_2 (and_2_out, cs, rd_en);
  GP_register gp_register_1 (
    .reg_in(data_in), .Reg_in_en(and_1_out), .Reg_clk(clk), .Reg_out_en(and_2_out), .Reg_in_out(mem_content),
    .Reg_out(data_out));
endmodule

module schemetic_RAM (
  input  sram_wr,
  input  sram_rd,
  input  [7:0] sram_d_in,
  input  [7:0] mar_d_in,
  input  MAR_in_en,
  input  sram_clk,
  output [7:0] sram_d_out,
  output [7:0] out_8,
  output [7:0] out_9,
  output [7:0] out_10,
  output [7:0] out_11,
  output [7:0] out_12,
  output [7:0] out_13,
  output [7:0] out_14,
  output [7:0] out_15,
  output [7:0] out_16,
  output [7:0] out_17,
  output [7:0] out_18,
  output [7:0] out_19,
  output [7:0] out_20,
  output [7:0] out_21,
  output [7:0] out_22,
  output [7:0] out_23
);

  wire [7:0] controlled_buffer_1_out, gp_register_1_reg_in_out;
  wire [15:0] dec_4_to_16_1_out_2;

  GP_register gp_register_1 (
    .reg_in(mar_d_in), .Reg_in_en(MAR_in_en), .Reg_clk(sram_clk), .Reg_in_out(gp_register_1_reg_in_out));  // open: Reg_out_en, Reg_out
  Dec_4_to_16 dec_4_to_16_1 (.in_1(gp_register_1_reg_in_out[3:0]), .out_2(dec_4_to_16_1_out_2));
  assign controlled_buffer_1_out = sram_wr ? sram_d_in : 8'bz;  // Controlled_Buffer controlled_buffer_1
  SRAM_cell sram_cell_1 (
    .data_in(controlled_buffer_1_out), .wr_in(sram_wr), .clk(sram_clk), .cs(dec_4_to_16_1_out_2[0]),
    .rd_en(sram_rd), .mem_content(out_8), .data_out(controlled_buffer_1_out));
  SRAM_cell sram_cell_2 (
    .data_in(controlled_buffer_1_out), .wr_in(sram_wr), .clk(sram_clk), .cs(dec_4_to_16_1_out_2[1]),
    .rd_en(sram_rd), .mem_content(out_9), .data_out(controlled_buffer_1_out));
  SRAM_cell sram_cell_3 (
    .data_in(controlled_buffer_1_out), .wr_in(sram_wr), .clk(sram_clk), .cs(dec_4_to_16_1_out_2[2]),
    .rd_en(sram_rd), .mem_content(out_10), .data_out(controlled_buffer_1_out));
  SRAM_cell sram_cell_4 (
    .data_in(controlled_buffer_1_out), .wr_in(sram_wr), .clk(sram_clk), .cs(dec_4_to_16_1_out_2[3]),
    .rd_en(sram_rd), .mem_content(out_11), .data_out(controlled_buffer_1_out));
  SRAM_cell sram_cell_5 (
    .data_in(controlled_buffer_1_out), .wr_in(sram_wr), .clk(sram_clk), .cs(dec_4_to_16_1_out_2[4]),
    .rd_en(sram_rd), .mem_content(out_12), .data_out(controlled_buffer_1_out));
  SRAM_cell sram_cell_6 (
    .data_in(controlled_buffer_1_out), .wr_in(sram_wr), .clk(sram_clk), .cs(dec_4_to_16_1_out_2[5]),
    .rd_en(sram_rd), .mem_content(out_13), .data_out(controlled_buffer_1_out));
  SRAM_cell sram_cell_7 (
    .data_in(controlled_buffer_1_out), .wr_in(sram_wr), .clk(sram_clk), .cs(dec_4_to_16_1_out_2[6]),
    .rd_en(sram_rd), .mem_content(out_14), .data_out(controlled_buffer_1_out));
  SRAM_cell sram_cell_8 (
    .data_in(controlled_buffer_1_out), .wr_in(sram_wr), .clk(sram_clk), .cs(dec_4_to_16_1_out_2[7]),
    .rd_en(sram_rd), .mem_content(out_15), .data_out(controlled_buffer_1_out));
  SRAM_cell sram_cell_9 (
    .data_in(controlled_buffer_1_out), .wr_in(sram_wr), .clk(sram_clk), .cs(dec_4_to_16_1_out_2[8]),
    .rd_en(sram_rd), .mem_content(out_16), .data_out(controlled_buffer_1_out));
  SRAM_cell sram_cell_10 (
    .data_in(controlled_buffer_1_out), .wr_in(sram_wr), .clk(sram_clk), .cs(dec_4_to_16_1_out_2[9]),
    .rd_en(sram_rd), .mem_content(out_17), .data_out(controlled_buffer_1_out));
  SRAM_cell sram_cell_11 (
    .data_in(controlled_buffer_1_out), .wr_in(sram_wr), .clk(sram_clk), .cs(dec_4_to_16_1_out_2[10]),
    .rd_en(sram_rd), .mem_content(out_18), .data_out(controlled_buffer_1_out));
  SRAM_cell sram_cell_12 (
    .data_in(controlled_buffer_1_out), .wr_in(sram_wr), .clk(sram_clk), .cs(dec_4_to_16_1_out_2[11]),
    .rd_en(sram_rd), .mem_content(out_19), .data_out(controlled_buffer_1_out));
  SRAM_cell sram_cell_13 (
    .data_in(controlled_buffer_1_out), .wr_in(sram_wr), .clk(sram_clk), .cs(dec_4_to_16_1_out_2[12]),
    .rd_en(sram_rd), .mem_content(out_20), .data_out(controlled_buffer_1_out));
  SRAM_cell sram_cell_14 (
    .data_in(controlled_buffer_1_out), .wr_in(sram_wr), .clk(sram_clk), .cs(dec_4_to_16_1_out_2[13]),
    .rd_en(sram_rd), .mem_content(out_21), .data_out(controlled_buffer_1_out));
  SRAM_cell sram_cell_15 (
    .data_in(controlled_buffer_1_out), .wr_in(sram_wr), .clk(sram_clk), .cs(dec_4_to_16_1_out_2[14]),
    .rd_en(sram_rd), .mem_content(out_22), .data_out(controlled_buffer_1_out));
  SRAM_cell sram_cell_16 (
    .data_in(controlled_buffer_1_out), .wr_in(sram_wr), .clk(sram_clk), .cs(dec_4_to_16_1_out_2[15]),
    .rd_en(sram_rd), .mem_content(out_23), .data_out(controlled_buffer_1_out));
  assign sram_d_out = sram_rd ? controlled_buffer_1_out : 8'bz;  // Controlled_Buffer controlled_buffer_2
endmodule

module schematic_IR (
  input  [7:0] ins_reg_in,
  input  ins_reg_in_en,
  input  clk,
  input  ins_reg_out_en,
  output [3:0] add_outs,
  output [3:0] ins_out
);

  wire [3:0] gp_register_1_reg_in_out;

  GP_register gp_register_1 (
    .reg_in(ins_reg_in), .Reg_in_en(ins_reg_in_en), .Reg_clk(clk),
    .Reg_in_out({ins_out, gp_register_1_reg_in_out}));  // open: Reg_out_en, Reg_out
  assign add_outs = ins_reg_out_en ? gp_register_1_reg_in_out : 4'bz;  // Controlled_Buffer controlled_buffer_1
endmodule

module SAP_1 (
  input  in_1,
  input  in_2,
  input  in_3,
  input  in_4,
  input  [7:0] in_5,
  input  in_6,
  input  Operating_mode,
  input  Code_upload_mode,
  input  in_9,
  input  in_10,
  output [7:0] out_11,
  output [7:0] out_12,
  output [7:0] out_13,
  output [7:0] out_14,
  output [7:0] out_15,
  output [7:0] out_16,
  output [7:0] out_17,
  output [7:0] out_18,
  output [7:0] out_19,
  output [7:0] out_20,
  output [7:0] out_21,
  output [7:0] out_22,
  output [3:0] out_23,
  output [7:0] out_24,
  output [7:0] out_25,
  output [7:0] out_26,
  output out_27,
  output [7:0] out_28,
  output out_29,
  output [7:0] out_30,
  output out_31,
  output out_32,
  output out_33,
  output out_34,
  output out_35,
  output [7:0] out_36
);

  wire a_in, a_out, alu_out, alu_sub, b_in, control_sequencer_1_mar_in_en, control_sequencer_1_pc_out_en,
       controlled_buffer_2_out, ins_reg_in_en, ins_reg_out_en, mar_in_en, pc_en, pc_out, sram_rd;
  wire [3:0] schematic_ir_1_ins_out;
  wire [7:0] gp_register_2_reg_in_out;

  Program_counter program_counter_1 (.in_1(pc_en), .PC_clk(in_6), .PC_reset(in_3), .pc_out_en(pc_out), .pc_out(out_23));
  schemetic_RAM schemetic_ram_1 (
    .sram_wr(in_2), .sram_rd(sram_rd), .sram_d_in({out_36[7:4], out_23}), .mar_d_in({out_36[7:4], out_23}),
    .MAR_in_en(mar_in_en), .sram_clk(in_6), .sram_d_out({out_36[7:4], out_23}), .out_8(out_12),
    .out_9(out_13), .out_10(out_14), .out_11(out_15), .out_12(out_16), .out_13(out_17), .out_14(out_18),
    .out_15(out_19), .out_16(out_20), .out_17(out_21), .out_18(out_22), .out_19(out_24), .out_20(out_25),
    .out_21(out_26), .out_22(out_28), .out_23(out_30));
  assign {out_36[7:4], out_23} = in_4 ? in_5 : 8'bz;  // Controlled_Buffer controlled_buffer_1
  GP_register gp_register_1 (
    .reg_in({out_36[7:4], out_23}), .Reg_in_en(a_in), .Reg_clk(in_6), .Reg_out_en(a_out),
    .Reg_in_out(out_11), .Reg_out({out_36[7:4], out_23}));
  GP_register gp_register_2 (
    .reg_in({out_36[7:4], out_23}), .Reg_in_en(b_in), .Reg_clk(in_6), .Reg_out_en(in_1),
    .Reg_in_out(gp_register_2_reg_in_out), .Reg_out({out_36[7:4], out_23}));
  schematic_IR schematic_ir_1 (
    .ins_reg_in({out_36[7:4], out_23}), .ins_reg_in_en(ins_reg_in_en), .clk(in_6),
    .ins_reg_out_en(ins_reg_out_en), .add_outs(out_23), .ins_out(schematic_ir_1_ins_out));
  ALU alu_1 (
    .alu_in_1(out_11), .alu_out_en(alu_out), .alu_sub(alu_sub), .alu_in_2(gp_register_2_reg_in_out),
    .alu_out({out_36[7:4], out_23}));  // open: alu_carry_out
  control_sequencer control_sequencer_1 (
    .i7(schematic_ir_1_ins_out[3]), .i6(schematic_ir_1_ins_out[2]), .I5(schematic_ir_1_ins_out[1]),
    .i4(schematic_ir_1_ins_out[0]), .clk(controlled_buffer_2_out), .reset(in_10), .T1(out_27), .T2(out_29),
    .T3(out_31), .T4(out_32), .T5(out_33), .T6(out_34), .HLT(out_35), .Pc_en(pc_en),
    .pc_out_en(control_sequencer_1_pc_out_en), .mar_in_en(control_sequencer_1_mar_in_en), .sram_rd(sram_rd),
    .IR_out_en(ins_reg_out_en), .IR_in_en(ins_reg_in_en), .a_in(a_in), .a_out(a_out), .alu_sub(alu_sub),
    .alu_out(alu_out), .b_in(b_in));
  assign controlled_buffer_2_out = Operating_mode ? in_6 : 1'bz;  // Controlled_Buffer controlled_buffer_2
  assign pc_out = Operating_mode ? control_sequencer_1_pc_out_en : 1'bz;  // Controlled_Buffer controlled_buffer_3
  assign mar_in_en = Operating_mode ? control_sequencer_1_mar_in_en : 1'bz;  // Controlled_Buffer controlled_buffer_4
  assign mar_in_en = Code_upload_mode ? in_9 : 1'bz;  // Controlled_Buffer controlled_buffer_5

  assign out_36[3:0] = out_23;

  // Other names for the same wires on the sheet: b_out = in_1; clk = in_6; debug = in_4; debug_data[7:0] = in_5;
  //   pc_reset = in_3; sram_wr = in_2
endmodule

module control_sequencer (
  input  i7,
  input  i6,
  input  I5,
  input  i4,
  input  clk,
  input  reset,
  output T1,
  output T2,
  output T3,
  output T4,
  output T5,
  output T6,
  output HLT,
  output Pc_en,
  output pc_out_en,
  output mar_in_en,
  output sram_rd,
  output IR_out_en,
  output IR_in_en,
  output a_in,
  output a_out,
  output alu_sub,
  output alu_out,
  output b_in
);

  wire and_1_out, and_2_out, and_3_out, and_4_out, and_6_out, and_7_out, and_9_out, and_10_out, j_k_ff_1_q,
       j_k_ff_2_qn, j_k_ff_3_qn, j_k_ff_4_qn, j_k_ff_5_qn, j_k_ff_6_qn, not_1_out, not_2_out, not_3_out,
       not_4_out, or_2_out, or_4_out, or_5_out, or_7_out, or_8_out, or_9_out;

  not not_1 (not_1_out, i7);
  not not_2 (not_2_out, i6);
  not not_3 (not_3_out, I5);
  not not_4 (not_4_out, i4);
  and and_1 (and_1_out, i4, not_3_out, not_2_out, not_1_out);
  and and_2 (and_2_out, not_4_out, I5, not_2_out, not_1_out);
  and and_3 (and_3_out, i4, I5, not_2_out, not_1_out);
  and and_4 (and_4_out, not_4_out, not_3_out, not_2_out, i7);
  and and_5 (HLT, i4, I5, i6, i7);
  J_K_Flip_Flop j_k_ff_1 (
    .J(j_k_ff_6_qn), .K(T6), .clk(clk), .Q(j_k_ff_1_q), .Qn(pc_out_en), .reset(reset));  // open: preset
  J_K_Flip_Flop j_k_ff_2 (
    .J(pc_out_en), .K(j_k_ff_1_q), .clk(clk), .Q(IR_in_en), .Qn(j_k_ff_2_qn), .reset(reset));  // open: preset
  J_K_Flip_Flop j_k_ff_3 (
    .J(IR_in_en), .K(j_k_ff_2_qn), .clk(clk), .Q(Pc_en), .Qn(j_k_ff_3_qn), .reset(reset));  // open: preset
  and and_6 (and_6_out, T4, or_2_out);
  or or_1 (mar_in_en, pc_out_en, and_6_out);
  or or_2 (or_2_out, and_1_out, and_2_out, and_3_out);
  J_K_Flip_Flop j_k_ff_4 (
    .J(Pc_en), .K(j_k_ff_3_qn), .clk(clk), .Q(T4), .Qn(j_k_ff_4_qn), .reset(reset));  // open: preset
  and and_7 (and_7_out, T5, or_4_out);
  or or_3 (sram_rd, IR_in_en, and_7_out);
  J_K_Flip_Flop j_k_ff_5 (.J(T4), .K(j_k_ff_4_qn), .clk(clk), .Q(T5), .Qn(j_k_ff_5_qn), .reset(reset));  // open: preset
  or or_4 (or_4_out, and_1_out, and_2_out, and_3_out, and_4_out);
  and and_8 (IR_out_en, T4, or_5_out);
  or or_5 (or_5_out, and_1_out, and_2_out, and_3_out);
  J_K_Flip_Flop j_k_ff_6 (.J(T5), .K(j_k_ff_5_qn), .clk(clk), .Q(T6), .Qn(j_k_ff_6_qn), .reset(reset));  // open: preset
  and and_9 (and_9_out, T5, and_1_out);
  or or_6 (a_in, and_9_out, and_10_out);
  or or_7 (or_7_out, and_2_out, and_3_out);
  and and_10 (and_10_out, T6, or_7_out);
  and and_11 (a_out, T4, and_4_out);
  and and_12 (alu_sub, T6, and_3_out);
  and and_13 (alu_out, T6, or_8_out);
  or or_8 (or_8_out, and_2_out, and_3_out);
  and and_14 (b_in, T5, or_9_out);
  or or_9 (or_9_out, and_2_out, and_3_out);

  assign T1 = pc_out_en;
  assign T2 = IR_in_en;
  assign T3 = Pc_en;

  // Notes on the sheet:
  //   LOAD
  //   ADD
  //   SUB
  //   OUT
endmodule
